// Logisim project full_adder_4bits.circ as structural Verilog: 1 circuit, main circuit main
module main (
  input  a0,
  input  b0,
  input  a1,
  input  b1,
  input  a2,
  input  b2,
  input  a3,
  input  b3,
  output out_9,
  output out_10,
  output out_11,
  output out_12,
  output c_out
);

  wire adder_1_cout, adder_2_cout, adder_3_cout;

  Adder #(.width(1)) adder_1 (.a(a0), .b(b0), .out(out_9), .cin(1'b0), .cout(adder_1_cout));
  Adder #(.width(1)) adder_2 (.a(a1), .b(b1), .out(out_10), .cin(adder_1_cout), .cout(adder_2_cout));
  Adder #(.width(1)) adder_3 (.a(a2), .b(b2), .out(out_11), .cin(adder_2_cout), .cout(adder_3_cout));
  Adder #(.width(1)) adder_4 (.a(a3), .b(b3), .out(out_12), .cin(adder_3_cout), .cout(c_out));
endmodule
