// Logisim project subtractor_4bits.circ as structural Verilog: 1 circuit, main circuit main
module main (
  input  a0,
  input  b0,
  input  a1,
  input  b1,
  input  a2,
  input  b2,
  input  a3,
  input  b3,
  output out_9,
  output out_10,
  output out_11,
  output out_12,
  output c_out__desprezar
);

  wire adder_1_cout, adder_2_cout, adder_3_cout, not_1_out, not_2_out, not_3_out, not_4_out;

  not not_1 (not_1_out, a0);
  not not_2 (not_2_out, a1);
  not not_3 (not_3_out, a2);
  not not_4 (not_4_out, a3);
  Adder #(.width(1)) adder_1 (.a(not_1_out), .b(b0), .out(out_9), .cin(1'b1), .cout(adder_1_cout));
  Adder #(.width(1)) adder_2 (.a(not_2_out), .b(b1), .out(out_10), .cin(adder_1_cout), .cout(adder_2_cout));
  Adder #(.width(1)) adder_3 (.a(not_3_out), .b(b2), .out(out_11), .cin(adder_2_cout), .cout(adder_3_cout));
  Adder #(.width(1)) adder_4 (.a(not_4_out), .b(b3), .out(out_12), .cin(adder_3_cout), .cout(c_out__desprezar));
endmodule
