// Logisim project counter.circ as structural Verilog: 1 circuit, main circuit main
module main (
  input  Ck,
  output out_2,
  output out_3,
  output a2
);

  J_K_Flip_Flop #(.trigger("falling")) j_k_ff_1 (
    .J(1'b1), .clk(Ck), .K(1'b1), .Q(out_2));  // open: Qn, preset, en, reset
  J_K_Flip_Flop #(.trigger("falling")) j_k_ff_2 (
    .J(1'b1), .clk(out_2), .K(1'b1), .Q(out_3));  // open: Qn, preset, en, reset
  J_K_Flip_Flop #(.trigger("falling")) j_k_ff_3 (
    .J(1'b1), .clk(out_3), .K(1'b1), .Q(a2));  // open: Qn, preset, en, reset

  // Notes on the sheet:
  //   a0
  //   a1
endmodule
