// Logisim project flipflopSR.circ as structural Verilog: 1 circuit, main circuit main
module main (
  input  S,
  input  Ck,
  input  R,
  output Q,
  output Q_2
);

  wire nand_1_out, nand_2_out, nand_3_out, nand_4_out, nand_5_out, nand_6_out, not_1_out;

  nand nand_1 (nand_1_out, S, Ck);
  nand nand_2 (nand_2_out, Ck, R);
  not not_1 (not_1_out, Ck);
  nand nand_3 (nand_3_out, nand_1_out, nand_4_out);
  nand nand_4 (nand_4_out, nand_3_out, nand_2_out);
  nand nand_5 (nand_5_out, nand_3_out, not_1_out);
  nand nand_6 (nand_6_out, not_1_out, nand_4_out);
  nand nand_7 (Q, nand_5_out, Q_2);
  nand nand_8 (Q_2, Q, nand_6_out);

  // Notes on the sheet:
  //   _
endmodule
