// Logisim project JKflipflopAsync.circ as structural Verilog: 1 circuit, main circuit main
module main (
  input  PRE,
  input  J,
  input  Ck,
  input  K,
  input  CLR,
  output out_6,
  output out_7
);

  wire nand_1_out, nand_2_out, nand_3_out, nand_4_out, nand_5_out, nand_6_out, not_1_out;

  nand nand_1 (nand_1_out, out_7, J, Ck);
  nand nand_2 (nand_2_out, Ck, K, out_6);
  not not_1 (not_1_out, Ck);
  nand nand_3 (nand_3_out, PRE, nand_1_out, nand_4_out);
  nand nand_4 (nand_4_out, nand_3_out, nand_2_out, CLR);
  nand nand_5 (nand_5_out, nand_3_out, not_1_out);
  nand nand_6 (nand_6_out, not_1_out, nand_4_out);
  nand nand_7 (out_6, PRE, nand_5_out, out_7);
  nand nand_8 (out_7, out_6, nand_6_out, CLR);
endmodule
