// Logisim project flipflopT.circ as structural Verilog: 1 circuit, main circuit main
module main (
  input  in_1,
  output out_2
);

  wire not_1_out;

  D_Flip_Flop #(.trigger("falling")) d_ff_1 (.clk(in_1), .D(not_1_out), .Q(out_2));  // open: Qn, preset, en, reset
  not not_1 (not_1_out, out_2);
endmodule
