// Logisim project gray_counter.circ as structural Verilog: 1 circuit, main circuit main
module main (
  input  Ck,
  output a2,
  output a1,
  output a0
);

  wire and_1_out, and_2_out, and_3_out, not_1_out, not_2_out;
  wire [2:0] xnor_1_out;

  Register #(.width(3)) register_1 (.D(xnor_1_out), .Q({a2, a1, a0}), .clk(Ck));  // open: en, clr
  not not_1 (not_1_out, a0);
  not not_2 (not_2_out, a2);
  or or_1 (xnor_1_out[1], and_1_out, and_2_out);
  xnor xnor_1 (xnor_1_out[0], a1, a2);
  and and_1 (and_1_out, a0, not_2_out);
  or or_2 (xnor_1_out[2], and_2_out, and_3_out);
  and and_2 (and_2_out, not_1_out, a1);
  and and_3 (and_3_out, a0, a2);

  // Notes on the sheet:
  //   A0
  //   A1
  //   A2
endmodule
