// Logisim project exemplo1_updown_gray.circ as structural Verilog: 3 circuits, main circuit main
module main (
  input  Ck,
  input  X,
  output Q1,
  output Q0
);

  wire xnor_1_out, xor_1_out;

  Flip_flop_D flip_flop_d_1 (.D(xnor_1_out), .Ck(Ck), .Q(Q1));  // open: Q_prime
  Flip_flop_D_2 flip_flop_d_2 (.D(xor_1_out), .Ck(Ck), .Q(Q0));  // open: Q_prime
  xor xor_1 (xor_1_out, Q1, X);
  xnor xnor_1 (xnor_1_out, X, Q0);

  // Notes on the sheet:
  //   Y0
  //   Y1
endmodule

module Flip_flop_D (
  input  D,
  input  Ck,
  output Q,
  output Q_prime
);

  D_Flip_Flop #(.trigger("falling")) d_ff_1 (.clk(Ck), .D(D), .Q(Q), .Qn(Q_prime));  // open: preset, en, reset
endmodule

module Flip_flop_D_2 (
  input  D,
  input  Ck,
  output Q,
  output Q_prime
);

  wire not_1_out;

  not not_1 (not_1_out, D);
  Flip_flop_D flip_flop_d_1 (.D(not_1_out), .Ck(Ck), .Q(Q_prime), .Q_prime(Q));
endmodule
