// Logisim project exemplo2_maquina_vendas_completo.circ as structural Verilog: 3 circuits, main circuit main
module main (
  input  Ck,
  input  X,
  output Refrigerante,
  output \Água 
);

  wire and_1_out, and_2_out, and_3_out, and_4_out, and_5_out, and_6_out, and_7_out, and_8_out,
       flip_flop_d_1_q_prime, flip_flop_d_2_q, flip_flop_d_2_q_prime, flip_flop_d_3_q, flip_flop_d_3_q_prime,
       not_1_out, or_2_out, or_3_out, or_4_out;

  Flip_flop_D flip_flop_d_1 (.D(or_4_out), .Ck(Ck), .Q(Refrigerante), .Q_prime(flip_flop_d_1_q_prime));
  Flip_flop_D flip_flop_d_2 (.D(or_3_out), .Ck(Ck), .Q(flip_flop_d_2_q), .Q_prime(flip_flop_d_2_q_prime));
  Flip_flop_D flip_flop_d_3 (.D(or_2_out), .Ck(Ck), .Q(flip_flop_d_3_q), .Q_prime(flip_flop_d_3_q_prime));
  not not_1 (not_1_out, X);
  and and_1 (and_1_out, flip_flop_d_2_q, flip_flop_d_3_q);
  or or_1 (\Água , Refrigerante, and_1_out);
  or or_2 (or_2_out, and_2_out, and_4_out);
  and and_2 (and_2_out, X, flip_flop_d_3_q, flip_flop_d_2_q_prime);
  and and_3 (and_3_out, flip_flop_d_3_q, flip_flop_d_2_q_prime);
  and and_4 (and_4_out, not_1_out, flip_flop_d_3_q_prime, flip_flop_d_1_q_prime);
  or or_3 (or_3_out, and_3_out, and_6_out, and_5_out);
  and and_5 (and_5_out, X, flip_flop_d_2_q_prime, flip_flop_d_1_q_prime);
  and and_6 (and_6_out, not_1_out, flip_flop_d_3_q_prime, flip_flop_d_2_q);
  or or_4 (or_4_out, and_8_out, Refrigerante, and_7_out);
  and and_7 (and_7_out, X, flip_flop_d_2_q);
  and and_8 (and_8_out, flip_flop_d_3_q, flip_flop_d_2_q);

  // Notes on the sheet:
  //   Q2
  //   Q1
  //   Q0
endmodule

module Flip_flop_D (
  input  D,
  input  Ck,
  output Q,
  output Q_prime
);

  D_Flip_Flop #(.trigger("falling")) d_ff_1 (.clk(Ck), .D(D), .Q(Q), .Qn(Q_prime));  // open: preset, en, reset
endmodule

module Flip_flop_D_2 (
  input  D,
  input  Ck,
  output Q,
  output Q_prime
);

  wire not_1_out;

  not not_1 (not_1_out, D);
  Flip_flop_D flip_flop_d_1 (.D(not_1_out), .Ck(Ck), .Q(Q_prime), .Q_prime(Q));
endmodule
