// Logisim project exemplo2_maquina_vendas_incompleto.circ as structural Verilog: 3 circuits, main circuit main
module main (
  input  Ck,
  input  X,
  output Q2,
  output Q1,
  output Q0
);

  wire and_1_out, and_2_out, and_3_out, and_4_out, and_5_out, and_6_out, and_7_out, flip_flop_d_1_q_prime,
       flip_flop_d_2_q_prime, flip_flop_d_3_q_prime, not_1_out, or_1_out, or_2_out, or_3_out;

  Flip_flop_D flip_flop_d_1 (.D(or_3_out), .Ck(Ck), .Q(Q2), .Q_prime(flip_flop_d_1_q_prime));
  Flip_flop_D flip_flop_d_2 (.D(or_2_out), .Ck(Ck), .Q(Q1), .Q_prime(flip_flop_d_2_q_prime));
  Flip_flop_D flip_flop_d_3 (.D(or_1_out), .Ck(Ck), .Q(Q0), .Q_prime(flip_flop_d_3_q_prime));
  not not_1 (not_1_out, X);
  or or_1 (or_1_out, and_1_out, and_3_out);
  and and_1 (and_1_out, X, Q0, flip_flop_d_2_q_prime);
  and and_2 (and_2_out, Q0, flip_flop_d_2_q_prime);
  and and_3 (and_3_out, not_1_out, flip_flop_d_3_q_prime, flip_flop_d_1_q_prime);
  or or_2 (or_2_out, and_2_out, and_5_out, and_4_out);
  and and_4 (and_4_out, X, flip_flop_d_2_q_prime, flip_flop_d_1_q_prime);
  and and_5 (and_5_out, not_1_out, flip_flop_d_3_q_prime, Q1);
  or or_3 (or_3_out, and_6_out, Q2, and_7_out);
  and and_6 (and_6_out, Q0, Q1);
  and and_7 (and_7_out, X, Q1);
endmodule

module Flip_flop_D (
  input  D,
  input  Ck,
  output Q,
  output Q_prime
);

  D_Flip_Flop #(.trigger("falling")) d_ff_1 (.clk(Ck), .D(D), .Q(Q), .Qn(Q_prime));  // open: preset, en, reset
endmodule

module Flip_flop_D_2 (
  input  D,
  input  Ck,
  output Q,
  output Q_prime
);

  wire not_1_out;

  not not_1 (not_1_out, D);
  Flip_flop_D flip_flop_d_1 (.D(not_1_out), .Ck(Ck), .Q(Q_prime), .Q_prime(Q));
endmodule
