// Logisim project irregular_counter.circ as structural Verilog: 3 circuits, main circuit main
module main (
  input  Ck,
  output Q2,
  output Q1,
  output Q0
);

  wire and_1_out, flip_flop_d_2_q_prime, flip_flop_d_3_q_prime, or_1_out, or_2_out;

  Flip_flop_D flip_flop_d_1 (.D(or_2_out), .Ck(Ck), .Q(Q2));  // open: Q_prime
  Flip_flop_D flip_flop_d_2 (.D(flip_flop_d_2_q_prime), .Ck(Ck), .Q(Q1), .Q_prime(flip_flop_d_2_q_prime));
  Flip_flop_D_2 flip_flop_d_3 (.D(or_1_out), .Ck(Ck), .Q(Q0), .Q_prime(flip_flop_d_3_q_prime));
  or or_1 (or_1_out, Q1, Q2);
  or or_2 (or_2_out, flip_flop_d_3_q_prime, and_1_out);
  and and_1 (and_1_out, flip_flop_d_2_q_prime, Q2);

  // Notes on the sheet:
  //   Y1
  //   Y0
  //   Y2
endmodule

module Flip_flop_D (
  input  D,
  input  Ck,
  output Q,
  output Q_prime
);

  D_Flip_Flop #(.trigger("falling")) d_ff_1 (.clk(Ck), .D(D), .Q(Q), .Qn(Q_prime));  // open: preset, en, reset
endmodule

module Flip_flop_D_2 (
  input  D,
  input  Ck,
  output Q,
  output Q_prime
);

  wire not_1_out;

  not not_1 (not_1_out, D);
  Flip_flop_D flip_flop_d_1 (.D(not_1_out), .Ck(Ck), .Q(Q_prime), .Q_prime(Q));
endmodule
