// Logisim project shift_register_serial_to_paralel.circ as structural Verilog: 3 circuits, main circuit main
module main (
  input  d,
  input  Ck,
  output Q3,
  output Q2,
  output Q1,
  output Q0
);

  Flip_flop_D flip_flop_d_1 (.D(d), .Ck(Ck), .Q(Q3));  // open: Q_prime
  Flip_flop_D flip_flop_d_2 (.D(Q3), .Ck(Ck), .Q(Q2));  // open: Q_prime
  Flip_flop_D flip_flop_d_3 (.D(Q2), .Ck(Ck), .Q(Q1));  // open: Q_prime
  Flip_flop_D flip_flop_d_4 (.D(Q1), .Ck(Ck), .Q(Q0));  // open: Q_prime
endmodule

module Flip_flop_D (
  input  D,
  input  Ck,
  output Q,
  output Q_prime
);

  D_Flip_Flop #(.trigger("falling")) d_ff_1 (.clk(Ck), .D(D), .Q(Q), .Qn(Q_prime));  // open: preset, en, reset
endmodule

module Flip_flop_D_2 (
  input  D,
  input  Ck,
  output Q,
  output Q_prime
);

  wire not_1_out;

  not not_1 (not_1_out, D);
  Flip_flop_D flip_flop_d_1 (.D(not_1_out), .Ck(Ck), .Q(Q_prime), .Q_prime(Q));
endmodule
