// Logisim project shiftreg_parallel_serial_evolution.circ as structural Verilog: 2 circuits, main circuit main
module main (
  input  d3,
  input  d2,
  input  d1,
  input  d0,
  input  SH_LD,
  output dout
);

  wire and_1_out, Ck_out, d_ff_1_q, d_ff_2_q, d_ff_3_q, mux_1_out, mux_2_out, mux_3_out;

  Clock Ck (.out(Ck_out));
  and and_1 (and_1_out, SH_LD, d3);
  D_Flip_Flop d_ff_1 (.D(and_1_out), .clk(Ck_out), .Q(d_ff_1_q));  // open: Qn, preset, reset
  mux mux_1 (.I0(d_ff_1_q), .I1(d2), .Out(mux_1_out), .Sel(SH_LD));
  D_Flip_Flop d_ff_2 (.D(mux_1_out), .clk(Ck_out), .Q(d_ff_2_q));  // open: Qn, preset, reset
  mux mux_2 (.I0(d_ff_2_q), .I1(d1), .Out(mux_2_out), .Sel(SH_LD));
  D_Flip_Flop d_ff_3 (.D(mux_2_out), .clk(Ck_out), .Q(d_ff_3_q));  // open: Qn, preset, reset
  mux mux_3 (.I0(d_ff_3_q), .I1(d0), .Out(mux_3_out), .Sel(SH_LD));
  D_Flip_Flop d_ff_4 (.D(mux_3_out), .clk(Ck_out), .Q(dout));  // open: Qn, preset, reset

  // Notes on the sheet:
  //   __
endmodule

module mux (
  input  I0,
  input  I1,
  input  Sel,
  output Out
);

  Multiplexer #(.enable("false")) multiplexer_1 (.in0(I0), .in1(I1), .out(Out), .sel(Sel));
endmodule
