// Logisim project shiftreg_serial_parallel_evolution.circ as structural Verilog: 1 circuit, main circuit main
module main (
  input  d,
  output Q3,
  output Q2,
  output Q1,
  output Q0
);

  wire Ck_out;

  Clock Ck (.out(Ck_out));
  D_Flip_Flop d_ff_1 (.D(d), .clk(Ck_out), .Q(Q3));  // open: Qn, preset, reset
  D_Flip_Flop d_ff_2 (.D(Q3), .clk(Ck_out), .Q(Q2));  // open: Qn, preset, reset
  D_Flip_Flop d_ff_3 (.D(Q2), .clk(Ck_out), .Q(Q1));  // open: Qn, preset, reset
  D_Flip_Flop d_ff_4 (.D(Q1), .clk(Ck_out), .Q(Q0));  // open: Qn, preset, reset
endmodule
