// Logisim project crazy_counter.circ as structural Verilog: 3 circuits, main circuit main
module main (
  input  Ck,
  output Q2,
  output Q1,
  output Q0
);

  wire flip_flop_j_k_2_q_prime;

  Flip_flop_J_K flip_flop_j_k_1 (.J(flip_flop_j_k_2_q_prime), .Ck(Ck), .Q(Q2), .K(1'b1));  // open: Q_prime
  Flip_flop_J_K flip_flop_j_k_2 (.J(Q2), .Ck(Ck), .Q(Q1), .Q_prime(flip_flop_j_k_2_q_prime), .K(1'b1));
  Flip_flop_J_K flip_flop_j_k_3 (.J(Q1), .Ck(Ck), .Q(Q0), .K(Q1));  // open: Q_prime
endmodule

module Flip_flop_D (
  input  D,
  input  Ck,
  output Q,
  output Q_prime
);

  D_Flip_Flop #(.trigger("falling")) d_ff_1 (.clk(Ck), .D(D), .Q(Q), .Qn(Q_prime));  // open: preset, en, reset
endmodule

module Flip_flop_J_K (
  input  J,
  input  Ck,
  input  K,
  output Q,
  output Q_prime
);

  J_K_Flip_Flop #(.trigger("falling")) j_k_ff_1 (
    .J(J), .clk(Ck), .K(K), .Q(Q), .Qn(Q_prime));  // open: preset, en, reset
endmodule
