// Logisim project exercicio2_maquina_de_vendas.circ as structural Verilog: 2 circuits, main circuit Parte Sequencial
module Parte_Sequencial (
  input  Ck,
  input  RST,
  input  A,
  input  B
);

  wire d_ff_1_q, d_ff_2_q, d_ff_3_q, not_1_out, parte_combinacional_1_y0, parte_combinacional_1_y1,
       parte_combinacional_1_y2;

  D_Flip_Flop #(.trigger("falling")) d_ff_1 (
    .clk(Ck), .D(parte_combinacional_1_y2), .Q(d_ff_1_q), .reset(not_1_out));  // open: Qn, preset, en
  not not_1 (not_1_out, RST);
  D_Flip_Flop #(.trigger("falling")) d_ff_2 (
    .clk(Ck), .D(parte_combinacional_1_y1), .Q(d_ff_2_q), .reset(not_1_out));  // open: Qn, preset, en
  D_Flip_Flop #(.trigger("falling")) d_ff_3 (
    .clk(Ck), .D(parte_combinacional_1_y0), .Q(d_ff_3_q), .reset(not_1_out));  // open: Qn, preset, en
  Parte_Combinacional parte_combinacional_1 (
    .A(A), .B(B), .Q2(d_ff_1_q), .Q1(d_ff_2_q), .Q0(d_ff_3_q), .Y2(parte_combinacional_1_y2),
    .Y1(parte_combinacional_1_y1), .Y0(parte_combinacional_1_y0));
endmodule

module Parte_Combinacional (
  input  A,
  input  B,
  input  Q2,
  input  Q1,
  input  Q0,
  output Y2,
  output Y1,
  output Y0
);

  wire and_1_out, and_2_out, and_3_out, and_4_out, and_5_out, and_6_out, and_7_out, and_8_out, and_9_out,
       and_10_out, nor_1_out, nor_2_out, not_1_out, not_2_out, not_3_out, not_4_out, not_5_out, not_6_out,
       not_7_out, not_8_out;

  and and_1 (and_1_out, Q1, Q0);
  and and_2 (and_2_out, B, Q1);
  not not_1 (not_1_out, A);
  not not_2 (not_2_out, Q1);
  not not_3 (not_3_out, B);
  not not_4 (not_4_out, Q0);
  not not_5 (not_5_out, Q1);
  not not_6 (not_6_out, Q2);
  not not_7 (not_7_out, Q2);
  not not_8 (not_8_out, Q1);
  or or_1 (Y2, and_1_out, Q2, and_2_out, A);
  and and_3 (and_3_out, not_1_out, not_2_out, Q0);
  and and_4 (and_4_out, not_3_out, Q1, not_4_out);
  and and_5 (and_5_out, B, not_5_out);
  and and_6 (and_6_out, B, Q2);
  and and_7 (and_7_out, A, Q1);
  and and_8 (and_8_out, A, Q2);
  nor nor_1 (nor_1_out, A, B, Q2, Q0);
  nor nor_2 (nor_2_out, A, B, Q1, Q0);
  and and_9 (and_9_out, B, not_6_out, Q0);
  and and_10 (and_10_out, A, not_7_out, not_8_out, Q0);
  or or_2 (Y1, and_3_out, and_4_out, and_5_out, and_6_out, and_7_out, and_8_out);
  or or_3 (Y0, nor_1_out, nor_2_out, and_9_out, and_10_out);
endmodule
