// Logisim project exercicio2_maquina_de_vendas_econ.circ as structural Verilog
module Parte_Combinacional (
  input  A,
  input  nQ2,
  input  Q2,
  input  nQ1,
  input  Q1,
  input  nQ0,
  input  Q0,
  input  B,
  output Y2,
  output Y1,
  output Y0
);

  wire and_1_out, and_2_out, and_3_out, and_4_out, and_5_out, and_6_out, and_7_out, and_8_out, and_9_out,
       and_10_out, and_11_out, and_12_out, not_1_out, not_2_out;

  not not_1 (not_1_out, A);
  not not_2 (not_2_out, B);
  and and_1 (and_1_out, Q1, Q0);
  and and_2 (and_2_out, B, Q1);
  and and_3 (and_3_out, not_1_out, nQ1, Q0);
  and and_4 (and_4_out, not_2_out, Q1, nQ0);
  and and_5 (and_5_out, B, nQ1);
  and and_6 (and_6_out, B, Q2);
  and and_7 (and_7_out, A, Q1);
  and and_8 (and_8_out, A, Q2);
  and and_9 (and_9_out, not_1_out, not_2_out, nQ2, nQ0);
  and and_10 (and_10_out, not_1_out, not_2_out, nQ1, nQ0);
  and and_11 (and_11_out, B, nQ2, Q0);
  and and_12 (and_12_out, A, nQ2, nQ1, Q0);
  or or_1 (Y2, and_1_out, Q2, and_2_out, A);
  or or_2 (Y0, and_9_out, and_10_out, and_11_out, and_12_out);
  or or_3 (Y1, and_3_out, and_4_out, and_5_out, and_6_out, and_7_out, and_8_out);
endmodule
