// Logisim project maquina_de_vendas2_logisim_evolution.circ as structural Verilog: 2 circuits, main circuit maquina_de_vendas2
module maquina_de_vendas2 (
  input  [1:0] moeda,
  output [2:0] estado,
  output Produto
);

  wire clock_1_out, parte_combinacional_1_y0, parte_combinacional_1_y1, parte_combinacional_1_y2, Reset_out;

  D_Flip_Flop d_ff_1 (
    .D(parte_combinacional_1_y0), .clk(clock_1_out), .Q(estado[0]), .reset(Reset_out));  // open: Qn, preset
  Clock clock_1 (.out(clock_1_out));
  Button Reset (.out(Reset_out));
  D_Flip_Flop d_ff_2 (
    .D(parte_combinacional_1_y1), .clk(clock_1_out), .Q(estado[1]), .reset(Reset_out));  // open: Qn, preset
  and and_1 (Produto, estado[1], estado[2]);
  D_Flip_Flop d_ff_3 (
    .D(parte_combinacional_1_y2), .clk(clock_1_out), .Q(estado[2]), .reset(Reset_out));  // open: Qn, preset
  parte_combinacional parte_combinacional_1 (
    .Y2(parte_combinacional_1_y2), .Y1(parte_combinacional_1_y1), .Y0(parte_combinacional_1_y0),
    .A(moeda[1]), .B(moeda[0]), .Q2(estado[2]), .Q1(estado[1]), .Q0(estado[0]));
endmodule

module parte_combinacional (
  input  A,
  input  B,
  input  Q2,
  input  Q1,
  input  Q0,
  output Y2,
  output Y1,
  output Y0
);

  wire and_1_out, and_2_out, and_3_out, and_4_out, and_5_out, and_6_out, and_7_out, and_8_out, and_9_out,
       and_10_out, and_11_out, and_12_out;

  and and_1 (and_1_out, Q1, Q0);
  and and_2 (and_2_out, B, Q1);
  and and_3 (and_3_out, ~A, ~Q1, Q0);  // AND_Gate
  and and_4 (and_4_out, ~B, Q1, ~Q0);  // AND_Gate
  and and_5 (and_5_out, B, ~Q1);  // AND_Gate
  and and_6 (and_6_out, B, Q2);
  and and_7 (and_7_out, A, Q1);
  and and_8 (and_8_out, A, Q2);
  and and_9 (and_9_out, ~A, ~B, ~Q2, ~Q0);  // AND_Gate
  and and_10 (and_10_out, ~A, ~B, ~Q1, ~Q0);  // AND_Gate
  and and_11 (and_11_out, B, ~Q2, Q0);  // AND_Gate
  and and_12 (and_12_out, A, ~Q2, ~Q1, Q0);  // AND_Gate
  or or_1 (Y2, and_1_out, Q2, and_2_out, A);
  or or_2 (Y1, and_3_out, and_4_out, and_5_out, and_6_out, and_7_out, and_8_out);
  or or_3 (Y0, and_9_out, and_10_out, and_11_out, and_12_out);
endmodule
