// Logisim project exemplo2_ok.circ as structural Verilog: 1 circuit, main circuit exemplo2
module exemplo2 (
  input  V,
  input  F,
  input  U,
  input  N,
  output \Chove_amanhã 
);

  wire and_1_out, and_2_out, and_3_out, and_4_out, and_5_out, not_1_out, not_2_out, not_3_out, not_4_out,
       not_5_out;

  not not_1 (not_1_out, F);
  not not_2 (not_2_out, U);
  not not_3 (not_3_out, V);
  not not_4 (not_4_out, N);
  not not_5 (not_5_out, V);
  and and_1 (and_1_out, V, not_1_out, not_2_out, N);
  and and_2 (and_2_out, not_3_out, F, N);
  and and_3 (and_3_out, V, U, not_4_out);
  and and_4 (and_4_out, not_5_out, U, N);
  and and_5 (and_5_out, F, U);
  or or_1 (\Chove_amanhã , and_1_out, and_2_out, and_3_out, and_4_out, and_5_out);
endmodule
