// Logisim project gray_counter.circ as structural Verilog: 2 circuits, main circuit main
module main (
  input  Ck,
  output a2,
  output a1,
  output a0
);

  wire and_1_out, and_2_out, and_3_out, not_1_out, not_2_out, or_1_out, or_2_out, xnor_1_out;

  Flip_flop_D flip_flop_d_1 (.D(or_2_out), .Ck(Ck), .Q(a2));  // open: Q_prime
  Flip_flop_D flip_flop_d_2 (.D(or_1_out), .Ck(Ck), .Q(a1));  // open: Q_prime
  not not_1 (not_1_out, a2);
  Flip_flop_D flip_flop_d_3 (.D(xnor_1_out), .Ck(Ck), .Q(a0));  // open: Q_prime
  xnor xnor_1 (xnor_1_out, a1, a2);
  not not_2 (not_2_out, a0);
  or or_1 (or_1_out, and_1_out, and_3_out);
  and and_1 (and_1_out, a0, not_1_out);
  or or_2 (or_2_out, and_3_out, and_2_out);
  and and_2 (and_2_out, a0, a2);
  and and_3 (and_3_out, not_2_out, a1);

  // Notes on the sheet:
  //   A0
  //   A1
  //   A2
endmodule

module Flip_flop_D (
  input  D,
  input  Ck,
  output Q,
  output Q_prime
);

  D_Flip_Flop d_ff_1 (.clk(Ck), .D(D), .Q(Q), .Qn(Q_prime));  // open: preset, en, reset
endmodule
